# Fritzing sketch Arduino Uno (saved by Fritzing 0.9.3b)
breadboards: 1

parts:
  U2 = LCD-16X2 [package=lcd-16x2_noholes]
  Componente1 = Arduino Uno (Rev3)
  R1 = Rotary Potentiometer (Large) [maximum_resistance=100kΩ package=THT]

nets:
  VSS: U2.VSS, U2.R_W, U2.K, Componente1.GND, R1.leg1
  VDD: U2.VDD, U2.A, Componente1.5V, R1.leg2
  N1: U2.VO, R1.wiper
  N2: U2.RS, Componente1.D12/MISO
  N3: U2.E, Componente1.D11_PWM/MOSI
  N4: U2.DB4, Componente1.D5_PWM
  N5: U2.DB5, Componente1.D4
  N6: U2.DB6, Componente1.D3_PWM
  N7: U2.DB7, Componente1.D2
