# Fritzing sketch Arduino uno com buzzer (saved by Fritzing 0.9.3b)
breadboards: 1

parts:
  U2 = LCD-16X2 [package=lcd-16x2_noholes]
  Componente1 = Arduino Uno (Rev3)
  R1 = Rotary Potentiometer (Large) [maximum_resistance=100kΩ package=THT]
  S1 = Pushbutton [package="[THT]"]
  S2 = Pushbutton [package="[THT]"]
  S3 = Pushbutton [package="[THT]"]
  R2 = Resistor [tolerance=±5% resistance=20k package="0402 [SMD]"]
  R3 = Resistor [tolerance=±5% resistance=20k package="0402 [SMD]"]
  R4 = Resistor [tolerance=±5% resistance=20k package="0402 [SMD]"]
  J1 = Piezo Speaker
  R5 = Rotary Potentiometer (Large) [maximum_resistance=100kΩ package=THT]

nets:
  VSS: U2.VSS, U2.R_W, U2.K, Componente1.GND, R1.leg1, R2.Pin_0, R3.Pin_0, R4.Pin_0, J1.pin1
  VDD: U2.VDD, U2.A, Componente1.5V, R1.leg2, S1.Pin_3, S1.Pin_4, S2.Pin_3, S2.Pin_4, S3.Pin_3, S3.Pin_4
  N1: U2.VO, R1.wiper
  N2: U2.RS, Componente1.D12/MISO
  N3: U2.E, Componente1.D11_PWM/MOSI
  N4: U2.DB4, Componente1.D4
  N5: U2.DB5, Componente1.D5_PWM
  N6: U2.DB6, Componente1.D3_PWM
  N7: U2.DB7, Componente1.D2
  N8: Componente1.D8, R5.leg1
  N9: Componente1.D9_PWM, S3.Pin_1, S3.Pin_2, R3.Pin_1
  N10: Componente1.D10_PWM/SS, S2.Pin_1, S2.Pin_2, R4.Pin_1
  N11: Componente1.D6_PWM, S1.Pin_1, S1.Pin_2, R2.Pin_1
  N12: J1.pin2, R5.wiper
